// Logisim project Controller.circ as structural Verilog: 1 circuit, main circuit main
module main (
  input  s,
  input  Ew_prime,
  input  Ew,
  input  El,
  input  El_prime,
  input  Foa,
  input  Ec_prime,
  input  Ec,
  input  Ef,
  input  Efo_prime,
  input  Efo,
  input  Gl,
  input  Reset,
  input  Clock,
  input  ResetScores,
  output Rcl,
  output Slc,
  output Cw,
  output Icl,
  output [3:0] State,
  output Iw,
  output Rw,
  output Sfoa,
  output Rfoa,
  output Ifo,
  output Ra,
  output Ifa,
  output [7:0] ComputerScoreBit,
  output [7:0] PlayerScoreBit
);

  wire and_2_out, and_3_out, and_4_out, and_5_out, and_6_out, and_7_out, and_8_out, and_9_out, and_10_out,
       and_11_out, and_12_out, and_13_out, and_14_out, and_15_out, and_16_out, and_17_out, and_18_out,
       and_19_out, and_20_out, and_21_out, and_22_out, and_23_out, and_24_out, and_25_out, and_26_out,
       and_27_out, and_28_out, and_29_out, and_30_out, and_31_out, and_32_out, and_33_out, and_34_out,
       and_35_out, and_36_out, and_37_out, and_38_out, and_39_out, and_40_out, and_41_out, and_42_out,
       and_43_out, and_44_out, and_45_out, and_46_out, and_47_out, and_49_out, and_50_out, and_51_out,
       and_52_out, and_53_out, and_54_out, and_55_out, and_56_out, and_57_out, and_58_out, and_60_out,
       and_61_out, and_62_out, and_63_out, and_66_out, and_67_out, and_68_out, and_69_out, and_70_out,
       and_71_out, and_72_out, and_73_out, and_75_out, and_76_out, and_78_out, and_79_out, and_80_out,
       and_81_out, and_82_out, and_83_out, and_85_out, and_86_out, and_87_out, not_1_out, not_2_out,
       not_3_out, not_4_out, not_5_out, not_6_out, not_7_out, not_8_out, not_9_out, not_10_out, not_11_out,
       not_12_out, not_13_out, not_14_out, not_15_out, not_16_out, not_17_out, not_18_out, not_19_out,
       not_20_out, not_21_out, not_22_out, not_23_out, not_24_out, not_25_out, not_26_out, not_27_out,
       not_28_out, not_29_out, not_30_out, not_31_out, not_32_out, not_33_out, not_34_out, not_35_out,
       not_36_out, not_37_out, not_38_out, not_39_out, not_40_out, not_41_out, not_42_out, not_43_out,
       not_44_out, not_45_out, not_46_out, not_47_out, not_48_out, not_49_out, not_50_out, not_51_out,
       not_52_out, not_53_out, not_54_out, not_55_out, not_56_out, not_57_out, not_58_out, not_59_out,
       not_60_out, not_61_out, not_62_out, not_63_out, not_64_out, not_65_out, not_66_out, not_67_out,
       not_68_out, not_69_out, not_70_out, not_71_out, not_72_out, not_73_out, not_74_out, not_75_out,
       not_76_out, not_77_out, not_78_out, not_79_out, not_80_out, not_81_out, not_82_out, not_83_out,
       not_84_out, not_85_out, not_86_out, not_87_out, not_88_out, not_89_out, not_90_out, not_91_out,
       not_92_out, not_93_out, not_94_out, not_95_out, not_96_out, not_97_out, not_98_out, not_99_out,
       not_100_out, not_101_out, not_102_out, not_103_out, not_104_out, not_105_out, not_106_out,
       not_107_out, not_108_out, not_109_out, not_110_out, not_111_out, not_112_out, not_113_out,
       not_114_out, not_115_out, not_116_out, not_117_out, not_118_out, not_119_out, not_120_out,
       not_121_out, not_122_out, not_123_out, not_124_out, not_125_out, not_126_out, not_127_out,
       not_128_out, not_129_out, not_130_out, not_131_out, not_132_out, not_133_out, not_134_out,
       not_135_out, not_136_out, not_137_out, not_138_out, not_139_out, not_140_out, not_141_out,
       not_142_out, not_143_out, not_144_out, not_145_out, not_146_out, not_147_out, not_148_out,
       not_149_out, not_150_out, not_151_out, not_152_out, not_153_out, not_154_out, not_155_out,
       not_156_out, not_157_out, not_158_out, not_159_out, not_160_out, not_161_out, not_162_out,
       not_163_out, not_164_out, not_165_out, not_166_out;
  wire [1:0] and_77_out, and_84_out, and_88_out, STATE_2_q, STATE_3_q, STATE_q;
  wire [3:0] counter_1_q, counter_2_q, or_4_out;
  wire [7:0] rom_1_data, rom_2_data;

  not not_1 (not_1_out, State[1]);
  not not_2 (not_2_out, State[1]);
  not not_3 (not_3_out, State[0]);
  not not_4 (not_4_out, State[2]);
  not not_5 (not_5_out, State[1]);
  not not_6 (not_6_out, State[3]);
  not not_7 (not_7_out, State[0]);
  not not_8 (not_8_out, State[1]);
  not not_9 (not_9_out, State[0]);
  not not_10 (not_10_out, State[3]);
  not not_11 (not_11_out, State[0]);
  not not_12 (not_12_out, State[3]);
  not not_13 (not_13_out, State[0]);
  not not_14 (not_14_out, State[3]);
  not not_15 (not_15_out, State[1]);
  not not_16 (not_16_out, State[1]);
  not not_17 (not_17_out, State[1]);
  not not_18 (not_18_out, State[0]);
  not not_19 (not_19_out, State[1]);
  not not_20 (not_20_out, Foa);
  not not_21 (not_21_out, State[1]);
  not not_22 (not_22_out, State[3]);
  not not_23 (not_23_out, State[0]);
  not not_24 (not_24_out, State[2]);
  not not_25 (not_25_out, State[3]);
  not not_26 (not_26_out, Gl);
  not not_27 (not_27_out, State[0]);
  not not_28 (not_28_out, State[1]);
  not not_29 (not_29_out, State[2]);
  not not_30 (not_30_out, State[1]);
  not not_31 (not_31_out, State[2]);
  not not_32 (not_32_out, State[1]);
  not not_33 (not_33_out, State[2]);
  not not_34 (not_34_out, State[0]);
  not not_35 (not_35_out, State[1]);
  not not_36 (not_36_out, State[2]);
  // AND_Gate and_1 has open pins: in0=Ew, in1=State[0], in2=not_1_out, in3=State[2], in4=State[3], out=open
  and and_2 (and_2_out, State[0], not_2_out, State[2], State[3]);
  and and_3 (and_3_out, Ef, not_3_out, State[1], not_4_out, State[3]);
  and and_4 (and_4_out, Foa, Ew, State[0], not_5_out, State[2], not_6_out);
  and and_5 (and_5_out, State[3], State[2], State[1], State[0]);
  and and_6 (and_6_out, not_7_out, not_8_out, State[2], State[3]);
  and and_7 (and_7_out, not_9_out, State[1], State[2], not_10_out);
  and and_8 (and_8_out, El, not_11_out, State[1], not_12_out);
  and and_9 (and_9_out, Ec_prime, not_13_out, State[1], not_14_out);
  and and_10 (and_10_out, Ew_prime, State[0], not_15_out, State[2]);
  and and_11 (and_11_out, Ew, State[0], not_16_out, State[2], State[3]);
  and and_12 (and_12_out, State[0], State[1], State[2], State[3]);
  and and_13 (and_13_out, Ew_prime, State[0], not_17_out, State[2], State[3]);
  and and_14 (and_14_out, not_18_out, not_19_out, State[2], State[3]);
  and and_15 (and_15_out, not_20_out, Ew, not_21_out, State[2], not_22_out);
  and and_16 (and_16_out, not_23_out, State[1], not_24_out, State[3]);
  and and_17 (and_17_out, State[0], State[1], State[2], not_25_out);
  and and_18 (and_18_out, not_26_out, not_27_out, not_28_out, not_29_out, State[3]);
  and and_19 (and_19_out, State[0], not_30_out, not_31_out, State[3]);
  and and_20 (and_20_out, State[0], not_32_out, State[2], State[3]);
  and and_21 (and_21_out, State[0], State[1], Ef, not_33_out, State[3]);
  and and_22 (and_22_out, Efo, not_34_out, not_35_out, not_36_out, State[3]);
  not not_37 (not_37_out, State[0]);
  not not_38 (not_38_out, State[2]);
  and and_23 (and_23_out, Efo, not_37_out, State[1], not_38_out, State[3]);
  or or_1 (or_4_out[2], and_2_out, and_3_out, and_4_out, and_5_out, and_6_out, and_7_out, and_8_out, and_9_out, and_10_out);
  or or_2 (or_4_out[3], and_23_out, and_11_out, and_12_out, and_13_out, and_14_out, and_15_out, and_20_out, and_16_out, and_17_out, and_18_out, and_19_out, and_21_out, and_22_out);
  Register #(.width(4)) State_Register (.D(or_4_out), .Q(State), .clk(Clock), .clr(Reset));  // open: en
  not not_39 (not_39_out, Gl);
  not not_40 (not_40_out, State[3]);
  not not_41 (not_41_out, State[2]);
  not not_42 (not_42_out, State[2]);
  and and_24 (and_24_out, State[3], not_41_out, not_39_out, State[1], State[0]);
  not not_43 (not_43_out, State[3]);
  not not_44 (not_44_out, State[1]);
  not not_45 (not_45_out, State[2]);
  and and_25 (and_25_out, not_40_out, not_42_out, not_44_out, State[0], Gl);
  not not_46 (not_46_out, State[0]);
  not not_47 (not_47_out, State[3]);
  not not_48 (not_48_out, State[2]);
  and and_26 (and_26_out, not_43_out, not_45_out, State[1], not_46_out, Ec, El_prime);
  not not_49 (not_49_out, State[3]);
  and and_27 (and_27_out, not_47_out, not_48_out, State[1], State[0]);
  and and_28 (and_28_out, not_49_out, State[2], not_53_out, not_52_out);
  not not_50 (not_50_out, State[1]);
  not not_51 (not_51_out, State[3]);
  not not_52 (not_52_out, State[0]);
  not not_53 (not_53_out, State[1]);
  and and_29 (and_29_out, not_51_out, State[2], not_50_out, State[0], Ew_prime);
  not not_54 (not_54_out, State[1]);
  not not_55 (not_55_out, State[3]);
  and and_30 (and_30_out, not_55_out, State[2], not_54_out, State[0], Ew, Foa);
  not not_56 (not_56_out, State[1]);
  not not_57 (not_57_out, State[3]);
  and and_31 (and_31_out, not_57_out, State[2], not_56_out, State[0], Ew, not_58_out);
  or or_3 (or_4_out[1], and_24_out, and_25_out, and_26_out, and_27_out, and_28_out, and_29_out, and_30_out, and_31_out, and_32_out, and_33_out, and_34_out, and_35_out);
  not not_58 (not_58_out, Foa);
  not not_59 (not_59_out, State[2]);
  not not_60 (not_60_out, State[1]);
  and and_32 (and_32_out, State[3], not_59_out, not_60_out, not_63_out, Gl);
  not not_61 (not_61_out, State[0]);
  not not_62 (not_62_out, State[2]);
  not not_63 (not_63_out, State[0]);
  and and_33 (and_33_out, State[3], not_62_out, State[1], not_61_out, not_64_out);
  not not_64 (not_64_out, Ef);
  not not_65 (not_65_out, State[2]);
  and and_34 (and_34_out, State[3], not_65_out, State[1], State[0], Gl);
  not not_66 (not_66_out, State[1]);
  and and_35 (and_35_out, State[3], State[2], not_66_out, State[0], Ew_prime);
  not not_67 (not_67_out, State[2]);
  not not_68 (not_68_out, State[1]);
  and and_36 (and_36_out, State[3], not_67_out, not_68_out, State[0]);
  not not_69 (not_69_out, State[1]);
  not not_70 (not_70_out, State[0]);
  not not_71 (not_71_out, State[2]);
  not not_72 (not_72_out, State[3]);
  and and_37 (and_37_out, not_72_out, not_71_out, not_69_out, not_70_out, s);
  not not_73 (not_73_out, State[2]);
  not not_74 (not_74_out, State[3]);
  not not_75 (not_75_out, State[0]);
  and and_38 (and_38_out, not_74_out, not_73_out, State[1], not_75_out, Ec, El_prime);
  not not_76 (not_76_out, State[3]);
  not not_77 (not_77_out, State[2]);
  not not_78 (not_78_out, State[0]);
  and and_39 (and_39_out, not_76_out, not_77_out, State[1], not_78_out, El);
  not not_79 (not_79_out, State[1]);
  not not_80 (not_80_out, State[3]);
  and and_40 (and_40_out, not_80_out, State[2], not_79_out, State[0], Ew, Foa);
  not not_81 (not_81_out, State[3]);
  not not_82 (not_82_out, State[0]);
  and and_41 (and_41_out, not_81_out, State[2], State[1], not_82_out);
  or or_4 (or_4_out[0], and_73_out, and_36_out, and_37_out, and_38_out, and_39_out, and_40_out, and_41_out, and_70_out, and_42_out, and_43_out, and_44_out, and_68_out, and_69_out, and_72_out, and_71_out, and_78_out, and_79_out, and_80_out);
  not not_83 (not_83_out, State[3]);
  and and_42 (and_42_out, not_83_out, State[2], State[1], State[0], Efo);
  not not_84 (not_84_out, State[2]);
  not not_85 (not_85_out, State[0]);
  not not_86 (not_86_out, Ef);
  and and_43 (and_43_out, State[3], not_84_out, State[1], not_85_out, not_86_out);
  not not_87 (not_87_out, State[3]);
  not not_88 (not_88_out, State[2]);
  not not_89 (not_89_out, State[1]);
  not not_90 (not_90_out, State[3]);
  not not_91 (not_91_out, State[2]);
  not not_92 (not_92_out, State[0]);
  not not_93 (not_93_out, State[3]);
  not not_94 (not_94_out, State[2]);
  not not_95 (not_95_out, State[1]);
  not not_96 (not_96_out, State[3]);
  not not_97 (not_97_out, State[2]);
  not not_98 (not_98_out, State[3]);
  not not_99 (not_99_out, State[3]);
  not not_100 (not_100_out, State[2]);
  not not_101 (not_101_out, State[1]);
  not not_102 (not_102_out, State[1]);
  not not_103 (not_103_out, State[0]);
  not not_104 (not_104_out, State[3]);
  not not_105 (not_105_out, State[2]);
  not not_106 (not_106_out, State[3]);
  not not_107 (not_107_out, State[1]);
  not not_108 (not_108_out, State[0]);
  not not_109 (not_109_out, State[3]);
  not not_110 (not_110_out, State[0]);
  not not_111 (not_111_out, State[3]);
  not not_112 (not_112_out, State[2]);
  not not_113 (not_113_out, State[1]);
  not not_114 (not_114_out, State[3]);
  not not_115 (not_115_out, State[2]);
  not not_116 (not_116_out, State[0]);
  not not_117 (not_117_out, State[3]);
  not not_118 (not_118_out, State[2]);
  not not_119 (not_119_out, State[3]);
  not not_120 (not_120_out, State[2]);
  not not_121 (not_121_out, State[0]);
  not not_122 (not_122_out, State[3]);
  not not_123 (not_123_out, State[2]);
  not not_124 (not_124_out, State[1]);
  not not_125 (not_125_out, State[2]);
  not not_126 (not_126_out, State[0]);
  not not_127 (not_127_out, State[3]);
  not not_128 (not_128_out, State[2]);
  not not_129 (not_129_out, State[1]);
  not not_130 (not_130_out, State[0]);
  not not_131 (not_131_out, State[2]);
  not not_132 (not_132_out, State[1]);
  not not_133 (not_133_out, State[1]);
  not not_134 (not_134_out, State[0]);
  not not_135 (not_135_out, State[0]);
  not not_136 (not_136_out, State[1]);
  and and_44 (and_44_out, State[3], State[2], not_136_out, not_135_out);
  and and_45 (and_45_out, not_87_out, not_88_out, not_89_out, State[0]);
  and and_46 (and_46_out, not_90_out, State[2], State[1], State[0]);
  and and_47 (and_47_out, State[3], not_91_out, State[1], not_92_out);
  and and_48 (Slc, not_93_out, not_94_out, not_95_out, State[0]);
  and and_49 (and_49_out, not_96_out, State[1], not_97_out, not_98_out);
  and and_50 (and_50_out, not_99_out, not_100_out, not_101_out, State[0]);
  and and_51 (and_51_out, State[3], State[2], not_102_out, not_103_out);
  and and_52 (and_52_out, not_104_out, not_105_out, State[1], State[0]);
  and and_53 (and_53_out, not_106_out, State[2], not_107_out, not_108_out);
  and and_54 (and_54_out, not_109_out, State[2], State[1], not_110_out);
  and and_55 (and_55_out, State[3], State[2], State[1], State[0]);
  and and_56 (and_56_out, not_111_out, not_112_out, not_113_out, State[0]);
  and and_57 (and_57_out, not_114_out, State[2], State[1], State[0]);
  and and_58 (and_58_out, State[3], not_115_out, State[1], not_116_out);
  and and_59 (Sfoa, not_117_out, not_118_out, State[1], State[0]);
  and and_60 (and_60_out, not_119_out, State[2], State[1], State[0]);
  and and_61 (and_61_out, State[3], not_120_out, State[1], not_121_out);
  and and_62 (and_62_out, not_122_out, not_123_out, not_124_out, State[0]);
  and and_63 (and_63_out, State[3], not_125_out, State[1], not_126_out);
  and and_64 (Ifo, not_127_out, not_128_out, State[1], State[0]);
  and and_65 (Ra, State[3], State[2], not_129_out, not_130_out);
  and and_66 (and_66_out, State[3], not_131_out, not_132_out, State[0]);
  and and_67 (and_67_out, State[3], State[2], not_133_out, not_134_out);
  not not_137 (not_137_out, State[1]);
  and and_68 (and_68_out, State[3], State[2], not_137_out, State[0], Ew_prime);
  or or_5 (Rcl, and_45_out, and_46_out, and_47_out);
  or or_6 (Cw, and_50_out, and_49_out, and_51_out);
  or or_7 (Icl, and_52_out, and_53_out);
  or or_8 (Iw, and_54_out, and_55_out);
  or or_9 (Rw, and_56_out, and_57_out, and_58_out);
  or or_10 (Rfoa, and_60_out, and_61_out, and_62_out);
  not not_138 (not_138_out, State[1]);
  not not_139 (not_139_out, State[2]);
  not not_140 (not_140_out, State[3]);
  and and_69 (and_69_out, State[3], State[2], State[1], State[0]);
  and and_70 (and_70_out, not_140_out, not_139_out, not_138_out, State[0], not_141_out);
  not not_141 (not_141_out, Gl);
  not not_142 (not_142_out, State[2]);
  not not_143 (not_143_out, State[1]);
  and and_71 (and_71_out, State[3], not_142_out, State[1], State[0], not_150_out);
  and and_72 (and_72_out, State[3], State[2], not_143_out, State[0]);
  not not_144 (not_144_out, STATE_q[1]);
  not not_145 (not_145_out, STATE_q[1]);
  not not_146 (not_146_out, STATE_q[0]);
  not not_147 (not_147_out, STATE_q[1]);
  not not_148 (not_148_out, STATE_q[0]);
  not not_149 (not_149_out, State[1]);
  not not_150 (not_150_out, Gl);
  and and_73 (and_73_out, State[3], State[2], not_149_out, State[0], Ew);
  and and_74 (Ifa, not_144_out, STATE_q[0]);
  and and_75 (and_75_out, and_63_out, not_145_out, STATE_q[0]);
  and and_76 (and_76_out, STATE_q[1], not_146_out, and_63_out);
  and and_77 (and_77_out[0], and_63_out, not_147_out, not_148_out);
  not not_151 (not_151_out, State[1]);
  not not_152 (not_152_out, State[2]);
  not not_153 (not_153_out, State[0]);
  not not_154 (not_154_out, State[2]);
  and and_78 (and_78_out, State[3], not_152_out, not_151_out, not_153_out, Efo);
  or or_11 (and_77_out[1], and_75_out, and_76_out);
  not not_155 (not_155_out, State[0]);
  not not_156 (not_156_out, State[2]);
  and and_79 (and_79_out, State[3], not_154_out, State[1], not_155_out, Efo);
  and and_80 (and_80_out, State[3], not_156_out, State[1], State[0], Ef);
  Register #(.width(2)) u_STATE (.D(and_77_out), .en(1'b1), .Q(STATE_q), .clk(Clock));  // open: clr
  and and_81 (and_81_out, not_157_out, STATE_2_q[0]);
  not not_157 (not_157_out, STATE_2_q[1]);
  and and_82 (and_82_out, and_66_out, not_158_out, STATE_2_q[0]);
  not not_158 (not_158_out, STATE_2_q[1]);
  not not_159 (not_159_out, STATE_2_q[0]);
  and and_83 (and_83_out, STATE_2_q[1], not_159_out, and_66_out);
  not not_160 (not_160_out, STATE_2_q[1]);
  and and_84 (and_84_out[0], and_66_out, not_160_out, not_161_out);
  not not_161 (not_161_out, STATE_2_q[0]);
  or or_12 (and_84_out[1], and_82_out, and_83_out);
  Register #(.width(2)) STATE_2 (.D(and_84_out), .en(1'b1), .Q(STATE_2_q), .clk(Clock));  // open: clr
  not not_162 (not_162_out, STATE_3_q[1]);
  not not_163 (not_163_out, STATE_3_q[1]);
  not not_164 (not_164_out, STATE_3_q[0]);
  not not_165 (not_165_out, STATE_3_q[1]);
  not not_166 (not_166_out, STATE_3_q[0]);
  and and_85 (and_85_out, not_162_out, STATE_3_q[0]);
  and and_86 (and_86_out, and_67_out, not_163_out, STATE_3_q[0]);
  and and_87 (and_87_out, STATE_3_q[1], not_164_out, and_67_out);
  and and_88 (and_88_out[0], and_67_out, not_165_out, not_166_out);
  or or_13 (and_88_out[1], and_86_out, and_87_out);
  Register #(.width(2)) STATE_3 (.D(and_88_out), .en(1'b1), .Q(STATE_3_q), .clk(Clock));  // open: clr
  Counter #(.width(4), .max('hf)) counter_1 (
    .count(and_81_out), .Q(counter_1_q), .clk(Clock), .clr(ResetScores));  // open: load, D, carry
  Counter #(.width(4), .max('hf)) counter_2 (
    .count(and_85_out), .Q(counter_2_q), .clk(Clock), .clr(ResetScores));  // open: load, D, carry
  Register #(.trigger("high")) register_1 (.D(rom_1_data), .Q(PlayerScoreBit), .clk(Clock));  // open: en, clr
  ROM #(.addrWidth(4)) rom_1 (.addr(counter_1_q), .data(rom_1_data));  // open: sel
  Register #(.trigger("high")) register_2 (.D(rom_2_data), .Q(ComputerScoreBit), .clk(Clock));  // open: en, clr
  ROM #(.addrWidth(4)) rom_2 (.addr(counter_2_q), .data(rom_2_data));  // open: sel

  // Notes on the sheet:
  //   Ew' Ew
  //   El El'   Foa
  //   Ec' Ec
  //   Efo' Efo
  //   Ef
  //   N2
  //   N3
  //   N1
  //   Ew' Ew
  //   El El'   Foa
  //   Ec' Ec
  //   Ef
  //   Efo' Efo
  //   N0
  //   Slc
  //   Sfoa
  //   Ifa
  //   Ifo
  //   Ra
  //   p
  //   c
  //   Rcl
  //   Cw
  //   Icl
  //   Iw
  //   Rw
  //   Rfoa
  //   Syncronizer
  //   Syncronizer
  //   Syncronizer
  //   7-Segment number binary storage
  //   contents of rom_1 (hex, n*v repeats v):
  //   3f 9 5e 5b 69 73 77 19 7f 79
  //   7-Segment number binary storage
  //   contents of rom_2 (hex, n*v repeats v):
  //   3f 9 5e 5b 69 73 77 19 7f 79
endmodule
