// Logisim project DataPath.circ as structural Verilog: 1 circuit, main circuit main
module main (
  input  CLOCK,
  input  A,
  input  B,
  input  C,
  input  D,
  input  E,
  input  F,
  input  G,
  input  H,
  input  I,
  input  J,
  input  K,
  input  L,
  input  M,
  input  N,
  input  O,
  input  P,
  input  Q,
  input  R,
  input  S,
  input  T,
  input  U,
  input  V,
  input  W,
  input  X,
  input  Y,
  input  Z,
  input  Start,
  input  Reset,
  input  Rcl,
  input  Slc,
  input  Cw,
  input  Icl,
  input  Iw,
  input  Rw,
  input  Sfoa,
  input  Rfoa,
  input  Ifa,
  input  Ifo,
  input  Ra,
  output Gl,
  output Ec,
  output Ec_prime,
  output Foa,
  output ClearDisplay,
  output Ef,
  output WriteNextLetter,
  output [6:0] DisplayWord,
  output El_prime,
  output El,
  output Efo,
  output Efo_prime,
  output [7:0] NumberOfLetters,
  output Ew,
  output Ew_prime,
  output [9:0] H0,
  output [9:0] H1,
  output [9:0] H2,
  output [9:0] H3,
  output [9:0] H4,
  output [9:0] H5,
  output [9:0] H6
);

  wire and_1_out, and_3_out, and_4_out, and_6_out, and_8_out, and_9_out, comparator_1_eq, comparator_2_eq,
       comparator_3_eq, comparator_4_eq, comparator_5_eq, comparator_6_eq, comparator_7_eq, comparator_8_eq,
       comparator_9_gt, comparator_9_lt, comparator_10_eq, comparator_11_eq, comparator_12_eq,
       comparator_13_eq, comparator_14_eq, comparator_15_eq, comparator_16_eq, comparator_17_eq,
       comparator_18_gt, comparator_18_lt, comparator_19_gt, comparator_19_lt, comparator_20_gt,
       comparator_20_lt, d_ff_1_q, d_ff_2_q, d_ff_3_q, d_ff_4_q, d_ff_5_q, d_ff_6_q, d_ff_7_q, d_ff_8_q,
       d_ff_9_q, d_ff_10_q, d_ff_21_q, d_ff_22_q, d_ff_23_q, d_ff_24_q, d_ff_25_q, d_ff_26_q, d_ff_27_q,
       d_ff_28_q, decoder_1_out1, decoder_1_out2, decoder_1_out3, decoder_1_out4, decoder_1_out5,
       decoder_1_out6, decoder_1_out7, decoder_1_out8, decoder_1_out9, decoder_1_out10, multiplexer_2_out,
       multiplexer_3_out, multiplexer_4_out, multiplexer_5_out, multiplexer_6_out, multiplexer_7_out,
       multiplexer_8_out, multiplexer_9_out, not_1_out, not_2_out, not_3_out, not_4_out, not_5_out,
       not_6_out, not_7_out, not_8_out, not_9_out, not_10_out, not_11_out, not_12_out, not_13_out,
       not_14_out, not_15_out, not_16_out, not_17_out, not_18_out, not_19_out, not_20_out, or_1_out,
       or_2_out, or_3_out, or_4_out, or_5_out, or_6_out, or_7_out, or_8_out, or_15_out, or_18_out, or_19_out,
       or_20_out, or_21_out, or_22_out, or_23_out, or_24_out, or_25_out;
  wire [1:0] and_5_out, and_10_out, STATE_2_q, STATE_q;
  wire [3:0] adder_1_out, adder_2_out, adder_3_out, adder_4_out, adder_5_out, adder_6_out, adder_7_out,
       adder_8_out, bit_extender_1_out, bit_extender_2_out, bit_extender_3_out, bit_extender_4_out,
       bit_extender_5_out, bit_extender_6_out, bit_extender_7_out, bit_extender_8_out, counter_1_q,
       CurrentLetterCounter_q, NumberOfFail_q, register_2_q, RegisterCounter_q, w_q;
  wire [4:0] or_10_out, ROM_AdressRegister_q;
  wire [7:0] demultiplexer_1_out1, demultiplexer_1_out2, demultiplexer_1_out3, demultiplexer_1_out4,
       demultiplexer_1_out5, demultiplexer_1_out6, demultiplexer_1_out7, demultiplexer_1_out8, Letter1_q,
       Letter2_q, Letter3_q, Letter4_q, Letter5_q, Letter6_q, Letter7_q, Letter8_q, multiplexer_1_out,
       multiplexer_10_out, multiplexer_11_out, multiplexer_12_out, multiplexer_13_out, multiplexer_14_out,
       multiplexer_15_out, multiplexer_16_out, multiplexer_17_out, multiplexer_18_out, multiplexer_19_out,
       rom_1_data, rom_2_data;

  assign bit_extender_1_out = {{3{1'b0}}, d_ff_2_q};  // Bit_Extender bit_extender_1
  assign bit_extender_2_out = {{3{1'b0}}, d_ff_3_q};  // Bit_Extender bit_extender_2
  assign bit_extender_3_out = {{3{1'b0}}, d_ff_4_q};  // Bit_Extender bit_extender_3
  assign bit_extender_4_out = {{3{1'b0}}, d_ff_5_q};  // Bit_Extender bit_extender_4
  assign bit_extender_5_out = {{3{1'b0}}, d_ff_6_q};  // Bit_Extender bit_extender_5
  assign bit_extender_6_out = {{3{1'b0}}, d_ff_7_q};  // Bit_Extender bit_extender_6
  assign bit_extender_7_out = {{3{1'b0}}, d_ff_8_q};  // Bit_Extender bit_extender_7
  assign bit_extender_8_out = {{3{1'b0}}, d_ff_9_q};  // Bit_Extender bit_extender_8
  D_Flip_Flop d_ff_1 (.Q(d_ff_1_q), .preset(Start), .reset(Reset));  // open: clk, D, Qn, en
  Multiplexer #(.width(8)) multiplexer_1 (
    .in0(8'h1), .in1(rom_2_data), .out(multiplexer_1_out), .sel(and_1_out));  // open: en
  and and_1 (and_1_out, Gl, d_ff_1_q);
  Adder #(.width(4)) adder_1 (.a(bit_extender_1_out), .b(bit_extender_2_out), .out(adder_1_out));  // open: cin, cout
  Adder #(.width(4)) adder_2 (.a(bit_extender_3_out), .b(bit_extender_4_out), .out(adder_2_out));  // open: cin, cout
  Adder #(.width(4)) adder_3 (.a(bit_extender_5_out), .b(bit_extender_6_out), .out(adder_3_out));  // open: cin, cout
  Adder #(.width(4)) adder_4 (.a(bit_extender_7_out), .b(bit_extender_8_out), .out(adder_4_out));  // open: cin, cout
  Adder #(.width(4)) adder_5 (.a(adder_1_out), .b(adder_2_out), .out(adder_5_out));  // open: cin, cout
  Adder #(.width(4)) adder_6 (.a(adder_3_out), .b(adder_4_out), .out(adder_6_out));  // open: cin, cout
  Comparator comparator_1 (.a(Letter1_q), .b(multiplexer_1_out), .eq(comparator_1_eq));  // open: gt, lt
  Comparator comparator_2 (.a(Letter2_q), .b(multiplexer_1_out), .eq(comparator_2_eq));  // open: gt, lt
  Comparator comparator_3 (.a(Letter3_q), .b(multiplexer_1_out), .eq(comparator_3_eq));  // open: gt, lt
  Comparator comparator_4 (.a(Letter4_q), .b(multiplexer_1_out), .eq(comparator_4_eq));  // open: gt, lt
  Comparator comparator_5 (.a(Letter5_q), .b(multiplexer_1_out), .eq(comparator_5_eq));  // open: gt, lt
  Comparator comparator_6 (.a(Letter6_q), .b(multiplexer_1_out), .eq(comparator_6_eq));  // open: gt, lt
  Comparator comparator_7 (.a(Letter7_q), .b(multiplexer_1_out), .eq(comparator_7_eq));  // open: gt, lt
  Comparator comparator_8 (.a(Letter8_q), .b(multiplexer_1_out), .eq(comparator_8_eq));  // open: gt, lt
  Adder #(.width(4)) adder_7 (.a(adder_5_out), .b(adder_6_out), .out(adder_7_out));  // open: cin, cout
  Multiplexer multiplexer_2 (.in0(1'b0), .in1(comparator_1_eq), .out(multiplexer_2_out), .sel(Gl));  // open: en
  Multiplexer multiplexer_3 (.in0(1'b0), .in1(comparator_2_eq), .out(multiplexer_3_out), .sel(Gl));  // open: en
  Multiplexer multiplexer_4 (.in0(1'b0), .in1(comparator_3_eq), .out(multiplexer_4_out), .sel(Gl));  // open: en
  Multiplexer multiplexer_5 (.in0(1'b0), .in1(comparator_4_eq), .out(multiplexer_5_out), .sel(Gl));  // open: en
  Multiplexer multiplexer_6 (.in0(1'b0), .in1(comparator_5_eq), .out(multiplexer_6_out), .sel(Gl));  // open: en
  Multiplexer multiplexer_7 (.in0(1'b0), .in1(comparator_6_eq), .out(multiplexer_7_out), .sel(Gl));  // open: en
  Multiplexer multiplexer_8 (.in0(1'b0), .in1(comparator_7_eq), .out(multiplexer_8_out), .sel(Gl));  // open: en
  Multiplexer multiplexer_9 (.in0(1'b0), .in1(comparator_8_eq), .out(multiplexer_9_out), .sel(Gl));  // open: en
  D_Flip_Flop d_ff_2 (.Q(d_ff_2_q), .preset(or_1_out), .reset(Reset));  // open: clk, D, Qn, en
  or or_1 (or_1_out, multiplexer_2_out, Ra);
  D_Flip_Flop d_ff_3 (.Q(d_ff_3_q), .preset(or_2_out), .reset(Reset));  // open: clk, D, Qn, en
  or or_2 (or_2_out, multiplexer_3_out, Ra);
  D_Flip_Flop d_ff_4 (.Q(d_ff_4_q), .preset(or_3_out), .reset(Reset));  // open: clk, D, Qn, en
  or or_3 (or_3_out, multiplexer_4_out, Ra);
  D_Flip_Flop d_ff_5 (.Q(d_ff_5_q), .preset(or_4_out), .reset(Reset));  // open: clk, D, Qn, en
  or or_4 (or_4_out, multiplexer_5_out, Ra);
  D_Flip_Flop d_ff_6 (.Q(d_ff_6_q), .preset(or_5_out), .reset(Reset));  // open: clk, D, Qn, en
  or or_5 (or_5_out, multiplexer_6_out, Ra);
  D_Flip_Flop d_ff_7 (.Q(d_ff_7_q), .preset(or_6_out), .reset(Reset));  // open: clk, D, Qn, en
  or or_6 (or_6_out, multiplexer_7_out, Ra);
  D_Flip_Flop d_ff_8 (.Q(d_ff_8_q), .preset(or_7_out), .reset(Reset));  // open: clk, D, Qn, en
  or or_7 (or_7_out, multiplexer_8_out, Ra);
  D_Flip_Flop d_ff_9 (.Q(d_ff_9_q), .preset(or_8_out), .reset(Reset));  // open: clk, D, Qn, en
  or or_8 (or_8_out, multiplexer_9_out, Ra);
  Multiplexer #(.width(8)) multiplexer_10 (
    .in0(8'h2d), .in1(Letter1_q), .out(multiplexer_10_out), .sel(d_ff_2_q));  // open: en
  Multiplexer #(.width(8)) multiplexer_11 (
    .in0(8'h2d), .in1(Letter2_q), .out(multiplexer_11_out), .sel(d_ff_3_q));  // open: en
  Multiplexer #(.width(8)) multiplexer_12 (
    .in0(8'h2d), .in1(Letter3_q), .out(multiplexer_12_out), .sel(d_ff_4_q));  // open: en
  Multiplexer #(.width(8)) multiplexer_13 (
    .in0(8'h2d), .in1(Letter4_q), .out(multiplexer_13_out), .sel(d_ff_5_q));  // open: en
  Multiplexer #(.width(8)) multiplexer_14 (
    .in0(8'h2d), .in1(Letter5_q), .out(multiplexer_14_out), .sel(d_ff_6_q));  // open: en
  Multiplexer #(.width(8)) multiplexer_15 (
    .in0(8'h2d), .in1(Letter6_q), .out(multiplexer_15_out), .sel(d_ff_7_q));  // open: en
  Multiplexer #(.width(8)) multiplexer_16 (
    .in0(8'h2d), .in1(Letter7_q), .out(multiplexer_16_out), .sel(d_ff_8_q));  // open: en
  Multiplexer #(.width(8)) multiplexer_17 (
    .in0(8'h2d), .in1(Letter8_q), .out(multiplexer_17_out), .sel(d_ff_9_q));  // open: en
  Counter #(.width(4), .max('hf)) u_w (.count(Iw), .Q(w_q), .clk(CLOCK), .clr(Rw));  // open: load, D, carry
  Multiplexer #(.select(4), .width(8)) multiplexer_18 (
    .in0(multiplexer_10_out), .in1(multiplexer_11_out), .in2(multiplexer_12_out), .in3(multiplexer_13_out),
    .in4(multiplexer_14_out), .in5(multiplexer_15_out), .in6(multiplexer_16_out), .in7(multiplexer_17_out),
    .out(multiplexer_18_out), .sel(w_q));  // open: in8, in9, in10, in11, in12, in13, in14, in15, en
  not not_1 (not_1_out, d_ff_1_q);
  Comparator #(.width(4)) comparator_9 (.a(w_q), .b(counter_1_q), .gt(comparator_9_gt), .eq(Ew), .lt(comparator_9_lt));
  Register #(.trigger("high")) register_1 (.D(rom_1_data), .Q(NumberOfLetters), .clk(not_1_out));  // open: en, clr
  ROM #(.addrWidth(4)) rom_1 (.addr(counter_1_q), .data(rom_1_data));  // open: sel
  or or_9 (Ew_prime, comparator_9_lt, comparator_9_gt);
  Bit_Extender #(.out_width(7)) bit_extender_9 (.in(multiplexer_18_out), .out(DisplayWord));
  or or_10 (or_10_out[0], A, C, E, G, I, K, M, O, Q, S, U, W, Y);
  or or_11 (or_10_out[1], B, C, F, G, J, K, N, O, R, S, V, W, Z);
  or or_12 (or_10_out[2], D, E, F, G, L, M, N, O, T, U, V, W);
  or or_13 (or_10_out[3], H, I, J, K, L, M, N, O, X, Y, Z);
  or or_14 (or_10_out[4], P, Q, R, S, T, U, V, W, X, Y, Z);
  or or_15 (or_15_out, or_10_out[0], or_10_out[1], or_10_out[2], or_10_out[3], or_10_out[4]);
  Register #(.width(5)) ROM_AdressRegister (.D(or_10_out), .Q(ROM_AdressRegister_q), .clk(or_15_out));  // open: en, clr
  not not_2 (not_2_out, STATE_q[1]);
  not not_3 (not_3_out, STATE_q[1]);
  not not_4 (not_4_out, STATE_q[0]);
  not not_5 (not_5_out, STATE_q[1]);
  not not_6 (not_6_out, STATE_q[0]);
  ROM #(.addrWidth(5)) rom_2 (.addr(ROM_AdressRegister_q), .data(rom_2_data));  // open: sel
  and and_2 (Gl, not_2_out, STATE_q[0]);
  and and_3 (and_3_out, or_15_out, not_3_out, STATE_q[0]);
  and and_4 (and_4_out, STATE_q[1], not_4_out, or_15_out);
  and and_5 (and_5_out[0], or_15_out, not_5_out, not_6_out);
  or or_16 (and_5_out[1], and_3_out, and_4_out);
  Demultiplexer #(.select(4), .width(8)) demultiplexer_1 (
    .out1(demultiplexer_1_out1), .out2(demultiplexer_1_out2), .out3(demultiplexer_1_out3),
    .out4(demultiplexer_1_out4), .out5(demultiplexer_1_out5), .out6(demultiplexer_1_out6),
    .out7(demultiplexer_1_out7), .out8(demultiplexer_1_out8), .in(rom_2_data), .sel(RegisterCounter_q));  // open: out0, out9, out10, out11, out12, out13, out14, out15, en
  Counter #(.width(4), .max('h9), .ongoal("stay")) RegisterCounter (
    .count(Gl), .Q(RegisterCounter_q), .clk(CLOCK), .clr(Reset));  // open: load, D, carry
  Register #(.width(2)) STATE (.D(and_5_out), .en(1'b1), .Q(STATE_q), .clk(CLOCK));  // open: clr
  D_Flip_Flop d_ff_10 (.Q(d_ff_10_q), .preset(Slc), .reset(Reset));  // open: clk, D, Qn, en
  not not_7 (not_7_out, d_ff_10_q);
  Decoder #(.select(4)) decoder_1 (
    .out1(decoder_1_out1), .out2(decoder_1_out2), .out3(decoder_1_out3), .out4(decoder_1_out4),
    .out5(decoder_1_out5), .out6(decoder_1_out6), .out7(decoder_1_out7), .out8(decoder_1_out8),
    .out9(decoder_1_out9), .out10(decoder_1_out10), .sel(NumberOfFail_q));  // open: out0, out11, out12, out13, out14, out15, en
  and and_6 (and_6_out, Gl, not_7_out);
  Comparator comparator_10 (.a(demultiplexer_1_out1), .b({8{1'b0}}), .eq(comparator_10_eq));  // open: gt, lt
  Comparator comparator_11 (.a(demultiplexer_1_out2), .b({8{1'b0}}), .eq(comparator_11_eq));  // open: gt, lt
  Comparator comparator_12 (.a(demultiplexer_1_out3), .b({8{1'b0}}), .eq(comparator_12_eq));  // open: gt, lt
  Comparator comparator_13 (.a(demultiplexer_1_out4), .b({8{1'b0}}), .eq(comparator_13_eq));  // open: gt, lt
  Comparator comparator_14 (.a(demultiplexer_1_out5), .b({8{1'b0}}), .eq(comparator_14_eq));  // open: gt, lt
  Comparator comparator_15 (.a(demultiplexer_1_out6), .b({8{1'b0}}), .eq(comparator_15_eq));  // open: gt, lt
  Comparator comparator_16 (.a(demultiplexer_1_out7), .b({8{1'b0}}), .eq(comparator_16_eq));  // open: gt, lt
  Comparator comparator_17 (.a(demultiplexer_1_out8), .b({8{1'b0}}), .eq(comparator_17_eq));  // open: gt, lt
  not not_8 (not_8_out, STATE_2_q[1]);
  not not_9 (not_9_out, STATE_2_q[1]);
  not not_10 (not_10_out, STATE_2_q[0]);
  D_Flip_Flop d_ff_11 (.Q(H0[9]), .preset(decoder_1_out1), .reset(Reset));  // open: clk, D, Qn, en
  D_Flip_Flop d_ff_12 (.Q(H1[9]), .preset(decoder_1_out2), .reset(Reset));  // open: clk, D, Qn, en
  D_Flip_Flop d_ff_13 (.Q(H3[9]), .preset(decoder_1_out3), .reset(Reset));  // open: clk, D, Qn, en
  D_Flip_Flop d_ff_14 (.Q(H5[9]), .preset(decoder_1_out4), .reset(Reset));  // open: clk, D, Qn, en
  D_Flip_Flop d_ff_15 (.Q(H3[8]), .preset(decoder_1_out5), .reset(Reset));  // open: clk, D, Qn, en
  D_Flip_Flop d_ff_16 (.Q(H2[7]), .preset(decoder_1_out6), .reset(Reset));  // open: clk, D, Qn, en
  D_Flip_Flop d_ff_17 (.Q(H3[4]), .preset(decoder_1_out7), .reset(Reset));  // open: clk, D, Qn, en
  D_Flip_Flop d_ff_18 (.Q(H2[0]), .preset(decoder_1_out8), .reset(Reset));  // open: clk, D, Qn, en
  D_Flip_Flop d_ff_19 (.Q(H2[3]), .preset(decoder_1_out9), .reset(Reset));  // open: clk, D, Qn, en
  D_Flip_Flop d_ff_20 (.Q(H4[3]), .preset(decoder_1_out10), .reset(Reset));  // open: clk, D, Qn, en
  D_Flip_Flop d_ff_21 (.Q(d_ff_21_q), .preset(not_11_out), .reset(Reset));  // open: clk, D, Qn, en
  not not_11 (not_11_out, comparator_10_eq);
  not not_12 (not_12_out, comparator_11_eq);
  D_Flip_Flop d_ff_22 (.Q(d_ff_22_q), .preset(not_12_out), .reset(Reset));  // open: clk, D, Qn, en
  not not_13 (not_13_out, comparator_12_eq);
  D_Flip_Flop d_ff_23 (.Q(d_ff_23_q), .preset(not_13_out), .reset(Reset));  // open: clk, D, Qn, en
  not not_14 (not_14_out, comparator_13_eq);
  D_Flip_Flop d_ff_24 (.Q(d_ff_24_q), .preset(not_14_out), .reset(Reset));  // open: clk, D, Qn, en
  D_Flip_Flop d_ff_25 (.Q(d_ff_25_q), .preset(not_15_out), .reset(Reset));  // open: clk, D, Qn, en
  not not_15 (not_15_out, comparator_14_eq);
  D_Flip_Flop d_ff_26 (.Q(d_ff_26_q), .preset(not_16_out), .reset(Reset));  // open: clk, D, Qn, en
  not not_16 (not_16_out, comparator_15_eq);
  not not_17 (not_17_out, comparator_16_eq);
  D_Flip_Flop d_ff_27 (.Q(d_ff_27_q), .preset(not_17_out), .reset(Reset));  // open: clk, D, Qn, en
  D_Flip_Flop d_ff_28 (.Q(d_ff_28_q), .preset(not_18_out), .reset(Reset));  // open: clk, D, Qn, en
  not not_18 (not_18_out, comparator_17_eq);
  // AND_Gate and_7 has open pins: in3=not_8_out, in4=STATE_2_q[0], out=open
  and and_8 (and_8_out, Ifo, not_9_out, STATE_2_q[0]);
  and and_9 (and_9_out, STATE_2_q[1], not_10_out, Ifo);
  not not_19 (not_19_out, STATE_2_q[1]);
  and and_10 (and_10_out[0], Ifo, not_19_out, not_20_out);
  not not_20 (not_20_out, STATE_2_q[0]);
  Counter #(.width(4), .max('h8), .ongoal("stay")) counter_1 (
    .count(and_6_out), .Q(counter_1_q), .clk(CLOCK), .clr(Reset));  // open: load, D, carry
  or or_17 (and_10_out[1], and_8_out, and_9_out);
  Register #(.width(4)) register_2 (.D(adder_7_out), .Q(register_2_q), .clk(CLOCK), .clr(Reset));  // open: en
  Register #(.width(2)) STATE_2 (.D(and_10_out), .en(1'b1), .Q(STATE_2_q), .clk(CLOCK));  // open: clr
  Register Letter1 (.D(demultiplexer_1_out1), .Q(Letter1_q), .clk(or_18_out), .clr(Reset));  // open: en
  or or_18 (or_18_out, d_ff_21_q, d_ff_1_q);
  Register Letter2 (.D(demultiplexer_1_out2), .Q(Letter2_q), .clk(or_19_out), .clr(Reset));  // open: en
  or or_19 (or_19_out, d_ff_22_q, d_ff_1_q);
  Register Letter3 (.D(demultiplexer_1_out3), .Q(Letter3_q), .clk(or_20_out), .clr(Reset));  // open: en
  or or_20 (or_20_out, d_ff_23_q, d_ff_1_q);
  Register Letter4 (.D(demultiplexer_1_out4), .Q(Letter4_q), .clk(or_21_out), .clr(Reset));  // open: en
  or or_21 (or_21_out, d_ff_24_q, d_ff_1_q);
  Register Letter5 (.D(demultiplexer_1_out5), .Q(Letter5_q), .clk(or_22_out), .clr(Reset));  // open: en
  or or_22 (or_22_out, d_ff_25_q, d_ff_1_q);
  Register Letter6 (.D(demultiplexer_1_out6), .Q(Letter6_q), .clk(or_23_out), .clr(Reset));  // open: en
  or or_23 (or_23_out, d_ff_26_q, d_ff_1_q);
  Register Letter7 (.D(demultiplexer_1_out7), .Q(Letter7_q), .clk(or_24_out), .clr(Reset));  // open: en
  or or_24 (or_24_out, d_ff_27_q, d_ff_1_q);
  Register Letter8 (.D(demultiplexer_1_out8), .Q(Letter8_q), .clk(or_25_out), .clr(Reset));  // open: en
  or or_25 (or_25_out, d_ff_28_q, d_ff_1_q);
  Comparator #(.width(4)) comparator_18 (
    .a(counter_1_q), .b(register_2_q), .gt(comparator_18_gt), .eq(Efo), .lt(comparator_18_lt));
  Counter #(.width(4), .max('hf), .ongoal("stay")) CurrentLetterCounter (
    .count(Icl), .Q(CurrentLetterCounter_q), .clk(CLOCK), .clr(Rcl));  // open: load, D, carry
  Multiplexer #(.select(4), .width(8)) multiplexer_19 (
    .in0({8{1'b1}}), .in1(Letter1_q), .in2(Letter2_q), .in3(Letter3_q), .in4(Letter4_q), .in5(Letter5_q),
    .in6(Letter6_q), .in7(Letter7_q), .in8(Letter8_q), .in9({8{1'b1}}), .in10({8{1'b1}}), .in11({8{1'b1}}),
    .in12({8{1'b1}}), .out(multiplexer_19_out), .sel(CurrentLetterCounter_q));  // open: in13, in14, in15, en
  Adder #(.width(4)) adder_8 (.a(counter_1_q), .b(4'b0001), .out(adder_8_out));  // open: cin, cout
  Comparator #(.width(4), .mode("unsigned")) comparator_19 (
    .a(CurrentLetterCounter_q), .b(adder_8_out), .gt(comparator_19_gt), .eq(El), .lt(comparator_19_lt));
  Comparator comparator_20 (
    .a(multiplexer_19_out), .b(rom_2_data), .gt(comparator_20_gt), .eq(Ec), .lt(comparator_20_lt));
  or or_26 (Efo_prime, comparator_18_gt, comparator_18_lt);
  or or_27 (Ec_prime, comparator_20_gt, comparator_20_lt);
  D_Flip_Flop LetterFound (.Q(Foa), .preset(Sfoa), .reset(Rfoa));  // open: clk, D, Qn, en
  Counter #(.width(4), .max('ha), .ongoal("stay")) NumberOfFail (
    .count(Ifa), .Q(NumberOfFail_q), .clk(CLOCK), .clr(Reset));  // open: load, D, carry
  or or_28 (El_prime, comparator_19_gt, comparator_19_lt);
  Comparator #(.width(4), .mode("unsigned")) comparator_21 (.a(NumberOfFail_q), .b(4'b1001), .eq(Ef));  // open: gt, lt

  assign ClearDisplay = Cw;
  assign H0[8:0] = {9{H0[9]}};
  assign {H2[9], H2[6:5]} = {H1[9], {2{H2[7]}}};
  assign {H3[7], H3[5], H3[3:1]} = {H3[8], H2[7], {3{H3[4]}}};
  assign {H4[9], H4[7:5], H4[0]} = {H3[9], {3{H2[7]}}, H2[0]};
  assign H6[9] = H5[9];
  assign WriteNextLetter = Iw;

  // Notes on the sheet:
  //   Ra
  //   StopCountLetter
  //   w = 0
  //   Cw(Clear)
  //   Rcl
  //   Sfoa
  //   Icl (increase current-letter-counter)
  //   Ifo (increase found number)
  //   w == Nl (Ew)
  //   w < Nl (Ew')
  //   7-Segment number binary storage
  //   contents of rom_1 (hex, n*v repeats v):
  //   3f 9 5e 5b 69 73 77 19 7f 79
  //   LetterROM
  //   contents of rom_2 (hex, n*v repeats v):
  //   0 61 62 63 64 65 66 67 68 69 6a 6b 6c 6d 6e 6f 70 71 72 73 74 75 76 77 78 79 7a
  //   Gl
  //   (GetLetter)
  //   Syncronizer
  //   NumberOfLetterCounter
  //   Syncronizer
  //   NumberOfFoundNumber
  //   Compares number of found letters and total letters
  //   Cn
  //   Increase number of fail
  //   Cmp == 1
  //   Efo
  //   Efo'
  //   Fa == 10 (Ef)
  //   Cl != Nl+1 (El')
  //   Cl == Nl+1 (El)
endmodule
