// Logisim project FinalProjectMain_161044065.circ as structural Verilog: 1 circuit, main circuit main
module main (
  output [3:0] STATE
);

  wire A_out, B_out, C_out, clock_1_out, D_out, E_out, F_out, G_out, H_out, I_out, J_out, K_out, L_out,
       M_out, main_1_cw, main_1_icl, main_1_ifa, main_1_ifo, main_1_iw, main_1_ra, main_1_rcl, main_1_rfoa,
       main_1_rw, main_1_sfoa, main_1_slc, main_2_cleardisplay, main_2_ec, main_2_ec_prime, main_2_ef,
       main_2_efo, main_2_efo_prime, main_2_el, main_2_el_prime, main_2_ew, main_2_ew_prime, main_2_foa,
       main_2_gl, main_2_writenextletter, N_out, O_out, P_out, Q_out, R_out, RESET_SCORES_out, RESTART_out,
       S_out, START_out, T_out, U_out, V_out, W_out, X_out, Y_out, Z_out;
  wire [6:0] main_2_displayword;
  wire [7:0] main_1_computerscorebit, main_1_playerscorebit, main_2_numberofletters;
  wire [9:0] main_2_h0, main_2_h1, main_2_h2, main_2_h3, main_2_h4, main_2_h5, main_2_h6;

  Clock clock_1 (.out(clock_1_out));
  Button RESET_SCORES (.out(RESET_SCORES_out));
  Button START (.out(START_out));
  Button RESTART (.out(RESTART_out));
  Controller_main main_1 (
    .Reset(RESTART_out), .Clock(clock_1_out), .State(STATE), .ResetScores(RESET_SCORES_out), .s(START_out),
    .Ew_prime(main_2_ew_prime), .Ew(main_2_ew), .El(main_2_el), .El_prime(main_2_el_prime), .Foa(main_2_foa),
    .Ec_prime(main_2_ec_prime), .Ec(main_2_ec), .Ef(main_2_ef), .Efo_prime(main_2_efo_prime),
    .Efo(main_2_efo), .Gl(main_2_gl), .Rcl(main_1_rcl), .Slc(main_1_slc), .Cw(main_1_cw), .Icl(main_1_icl),
    .Iw(main_1_iw), .Rw(main_1_rw), .Sfoa(main_1_sfoa), .Rfoa(main_1_rfoa), .Ifo(main_1_ifo), .Ra(main_1_ra),
    .Ifa(main_1_ifa), .ComputerScoreBit(main_1_computerscorebit), .PlayerScoreBit(main_1_playerscorebit));
  _7_Segment_Display u_7_segment_display_1 (
    .g(main_1_playerscorebit[6]), .f(main_1_playerscorebit[5]), .a(main_1_playerscorebit[4]),
    .b(main_1_playerscorebit[3]), .e(main_1_playerscorebit[2]), .d(main_1_playerscorebit[1]),
    .c(main_1_playerscorebit[0]));  // open: dp
  _7_Segment_Display u_7_segment_display_2 (
    .g(main_2_numberofletters[6]), .f(main_2_numberofletters[5]), .a(main_2_numberofletters[4]),
    .b(main_2_numberofletters[3]), .e(main_2_numberofletters[2]), .d(main_2_numberofletters[1]),
    .c(main_2_numberofletters[0]));  // open: dp
  _7_Segment_Display u_7_segment_display_3 (
    .g(main_1_computerscorebit[6]), .f(main_1_computerscorebit[5]), .a(main_1_computerscorebit[4]),
    .b(main_1_computerscorebit[3]), .e(main_1_computerscorebit[2]), .d(main_1_computerscorebit[1]),
    .c(main_1_computerscorebit[0]));  // open: dp
  Button B (.out(B_out));
  Button A (.out(A_out));
  Button E (.out(E_out));
  Button C (.out(C_out));
  Button D (.out(D_out));
  Button F (.out(F_out));
  Button G (.out(G_out));
  Button I (.out(I_out));
  Button H (.out(H_out));
  Button J (.out(J_out));
  Button K (.out(K_out));
  Button M (.out(M_out));
  Button L (.out(L_out));
  Button O (.out(O_out));
  Button N (.out(N_out));
  DataPath_main main_2 (
    .Gl(main_2_gl), .Reset(RESTART_out), .Rcl(main_1_rcl), .ClearDisplay(main_2_cleardisplay),
    .Slc(main_1_slc), .WriteNextLetter(main_2_writenextletter), .DisplayWord(main_2_displayword),
    .Cw(main_1_cw), .Icl(main_1_icl), .Iw(main_1_iw), .NumberOfLetters(main_2_numberofletters),
    .Rw(main_1_rw), .Sfoa(main_1_sfoa), .Rfoa(main_1_rfoa), .Ifa(main_1_ifa), .Ifo(main_1_ifo),
    .Ra(main_1_ra), .CLOCK(clock_1_out), .A(A_out), .B(B_out), .C(C_out), .D(D_out), .E(E_out), .F(F_out),
    .G(G_out), .H(H_out), .I(I_out), .J(J_out), .K(K_out), .L(L_out), .M(M_out), .N(N_out), .O(O_out),
    .P(P_out), .Q(Q_out), .R(R_out), .S(S_out), .T(T_out), .U(U_out), .V(V_out), .W(W_out), .X(X_out),
    .Y(Y_out), .Z(Z_out), .Ec(main_2_ec), .Ec_prime(main_2_ec_prime), .Foa(main_2_foa), .Start(START_out),
    .Ef(main_2_ef), .El_prime(main_2_el_prime), .El(main_2_el), .Efo(main_2_efo),
    .Efo_prime(main_2_efo_prime), .Ew(main_2_ew), .Ew_prime(main_2_ew_prime), .H0(main_2_h0), .H1(main_2_h1),
    .H2(main_2_h2), .H3(main_2_h3), .H4(main_2_h4), .H5(main_2_h5), .H6(main_2_h6));
  Button Q (.out(Q_out));
  Button R (.out(R_out));
  Button P (.out(P_out));
  TTY tty_1 (.data(main_2_displayword), .clk(main_2_writenextletter), .clr(main_2_cleardisplay));  // open: we
  Button T (.out(T_out));
  Button U (.out(U_out));
  Button S (.out(S_out));
  Button W (.out(W_out));
  Button V (.out(V_out));
  DotMatrix #(.matrixcols(7), .matrixrows(10)) dotmatrix_1 (
    .col0(main_2_h0), .col1(main_2_h1), .col2(main_2_h2), .col3(main_2_h3), .col4(main_2_h4),
    .col5(main_2_h5), .col6(main_2_h6));
  Button X (.out(X_out));
  Button Z (.out(Z_out));
  Button Y (.out(Y_out));

  // Notes on the sheet:
  //   PLAYER SCORE
  //   NUMBER OF LETTER THAT ENTERED
  //   COMPUTER SCORE
  //   THEN PRESS THE START BUTTON AND AFTER THAT PRESS THE LETTER THAT YOU WANT TO PREDICT
  //   256Hz CLOCK FREQUENCY VERY GOOD TO AVOID THAT PROBLEM 
  //   FIRST ENTER THE WORD. YOU CAN SEE HOW MANY LETTERS YOU ENTERED AT THE LEFT-TOP 7-SEGMENT DISPLAY
  //   PLEASE WAIT UNTIL IT DISPLAYES ALL THE WORD TO ENTER NEW LETTER
  //   AFTER WIN OR LOSE, FIRST PRESS THE RESTART BUTTON.THEN ENTER THE NEW WORD AND AFTER THAT PRESS THE START BUTTON AGAIN TO BEGIN NEW GAME
  //   AFTER YOU PREDICT A LETTER. IT CAN TAKE 1-1.5 SEC IF YOU PREDICT A WRONG ONE. OTHERWISE BUG OCCURS
  //   DISPLAY
  //   HANGSMAN DISPLAY
endmodule
