// Logisim project GameCircuit.circ as structural Verilog: 1 circuit, main circuit main
module main (
);

  wire and_1_out, and_2_out, and_3_out, and_5_out, and_6_out, and_7_out, and_9_out, and_10_out, and_11_out,
       and_13_out, and_14_out, and_15_out, and_17_out, and_18_out, and_19_out, and_20_out, and_21_out,
       and_22_out, and_23_out, and_24_out, and_25_out, and_26_out, and_27_out, and_28_out, and_29_out,
       and_30_out, and_31_out, and_32_out, and_33_out, B1_out, B2_out, button_1_out, clock_1_out,
       clock_2_out, clock_3_out, clock_4_out, clock_5_out, clock_6_out, clock_7_out, decoder_1_out0,
       decoder_1_out1, decoder_1_out2, decoder_1_out3, decoder_1_out4, decoder_1_out6, decoder_1_out7,
       not_1_out, not_2_out, not_3_out, not_4_out, not_5_out, not_6_out, not_7_out, not_8_out, not_9_out,
       not_10_out, not_11_out, not_12_out, not_13_out, not_14_out, not_15_out, not_16_out, not_17_out,
       not_18_out, not_19_out, not_20_out, not_21_out, not_22_out, not_23_out, not_24_out, not_25_out,
       not_26_out, not_27_out, not_28_out, not_29_out, not_30_out, not_31_out, not_32_out, not_33_out,
       not_34_out, not_35_out, not_36_out, not_37_out, not_38_out, not_39_out, not_40_out, not_41_out,
       not_42_out, not_43_out, not_44_out, not_45_out, not_46_out, not_47_out, not_48_out, not_49_out,
       not_50_out, not_51_out, not_52_out, not_53_out, not_54_out, not_55_out, not_56_out, not_57_out,
       not_58_out, R_out;
  wire [1:0] and_4_out, and_8_out, and_12_out, and_16_out, STATE_2_q, STATE_3_q, STATE_4_q, STATE_q;
  wire [2:0] or_7_out, STATE_5_q;
  wire [3:0] counter_1_q, counter_2_q;

  Button B1 (.out(B1_out));
  Button B2 (.out(B2_out));
  Button R (.out(R_out));
  not not_1 (not_1_out, STATE_q[1]);
  not not_2 (not_2_out, STATE_q[1]);
  not not_3 (not_3_out, STATE_q[0]);
  not not_4 (not_4_out, STATE_q[1]);
  not not_5 (not_5_out, STATE_q[0]);
  not not_6 (not_6_out, STATE_2_q[1]);
  not not_7 (not_7_out, STATE_2_q[1]);
  not not_8 (not_8_out, STATE_2_q[0]);
  not not_9 (not_9_out, STATE_3_q[1]);
  not not_10 (not_10_out, STATE_3_q[1]);
  not not_11 (not_11_out, STATE_3_q[0]);
  and and_1 (and_1_out, not_1_out, STATE_q[0]);
  and and_2 (and_2_out, B1_out, not_2_out, STATE_q[0]);
  and and_3 (and_3_out, STATE_q[1], not_3_out, B1_out);
  and and_4 (and_4_out[0], B1_out, not_4_out, not_5_out);
  and and_5 (and_5_out, not_6_out, STATE_2_q[0]);
  and and_6 (and_6_out, B2_out, not_7_out, STATE_2_q[0]);
  and and_7 (and_7_out, STATE_2_q[1], not_8_out, B2_out);
  not not_12 (not_12_out, STATE_2_q[1]);
  and and_8 (and_8_out[0], B2_out, not_12_out, not_13_out);
  not not_13 (not_13_out, STATE_2_q[0]);
  and and_9 (and_9_out, not_9_out, STATE_3_q[0]);
  and and_10 (and_10_out, and_32_out, not_10_out, STATE_3_q[0]);
  and and_11 (and_11_out, STATE_3_q[1], not_11_out, and_32_out);
  and and_12 (and_12_out[0], and_32_out, not_14_out, not_15_out);
  not not_14 (not_14_out, STATE_3_q[1]);
  not not_15 (not_15_out, STATE_3_q[0]);
  and and_13 (and_13_out, not_16_out, STATE_4_q[0]);
  not not_16 (not_16_out, STATE_4_q[1]);
  and and_14 (and_14_out, and_33_out, not_17_out, STATE_4_q[0]);
  not not_17 (not_17_out, STATE_4_q[1]);
  not not_18 (not_18_out, STATE_4_q[0]);
  and and_15 (and_15_out, STATE_4_q[1], not_18_out, and_33_out);
  not not_19 (not_19_out, STATE_4_q[1]);
  and and_16 (and_16_out[0], and_33_out, not_19_out, not_20_out);
  not not_20 (not_20_out, STATE_4_q[0]);
  or or_1 (and_4_out[1], and_2_out, and_3_out);
  or or_2 (and_8_out[1], and_6_out, and_7_out);
  or or_3 (and_12_out[1], and_10_out, and_11_out);
  or or_4 (and_16_out[1], and_14_out, and_15_out);
  Register #(.width(2)) STATE (.D(and_4_out), .en(1'b1), .Q(STATE_q), .clk(clock_1_out));  // open: clr
  Clock clock_1 (.out(clock_1_out));
  Clock clock_2 (.out(clock_2_out));
  Clock clock_3 (.out(clock_3_out));
  Clock clock_4 (.out(clock_4_out));
  Register #(.width(2)) STATE_2 (.D(and_8_out), .en(1'b1), .Q(STATE_2_q), .clk(clock_2_out));  // open: clr
  Register #(.width(2)) STATE_3 (.D(and_12_out), .en(1'b1), .Q(STATE_3_q), .clk(clock_3_out));  // open: clr
  Register #(.width(2)) STATE_4 (.D(and_16_out), .en(1'b1), .Q(STATE_4_q), .clk(clock_4_out));  // open: clr
  Clock clock_5 (.out(clock_5_out));
  Hex_Digit_Display hex_digit_display_1 (.value(counter_1_q));  // open: dp
  Counter #(.width(4), .max('h9)) counter_1 (
    .count(and_9_out), .Q(counter_1_q), .clk(clock_5_out), .clr(button_1_out));  // open: load, D, carry
  Button button_1 (.out(button_1_out));
  not not_21 (not_21_out, STATE_5_q[1]);
  not not_22 (not_22_out, STATE_5_q[0]);
  not not_23 (not_23_out, and_5_out);
  not not_24 (not_24_out, R_out);
  not not_25 (not_25_out, STATE_5_q[0]);
  not not_26 (not_26_out, and_5_out);
  not not_27 (not_27_out, R_out);
  not not_28 (not_28_out, STATE_5_q[0]);
  not not_29 (not_29_out, R_out);
  not not_30 (not_30_out, R_out);
  Hex_Digit_Display hex_digit_display_2 (.value(counter_2_q));  // open: dp
  Counter #(.width(4), .max('h9)) counter_2 (
    .count(and_13_out), .Q(counter_2_q), .clk(clock_6_out), .clr(button_1_out));  // open: load, D, carry
  Clock clock_6 (.out(clock_6_out));
  and and_17 (and_17_out, not_21_out, not_22_out, and_1_out, not_23_out, not_24_out);
  and and_18 (and_18_out, STATE_5_q[2], not_25_out, not_26_out, not_27_out);
  and and_19 (and_19_out, STATE_5_q[2], not_28_out, and_1_out, not_29_out);
  and and_20 (and_20_out, STATE_5_q[2], STATE_5_q[1], not_30_out);
  Register #(.width(3)) STATE_5 (.D(or_7_out), .en(1'b1), .Q(STATE_5_q), .clk(clock_7_out));  // open: clr
  Clock clock_7 (.out(clock_7_out));
  or or_5 (or_7_out[2], and_17_out, and_18_out, and_19_out, and_20_out);
  not not_31 (not_31_out, R_out);
  not not_32 (not_32_out, and_1_out);
  not not_33 (not_33_out, STATE_5_q[2]);
  and and_21 (and_21_out, not_33_out, STATE_5_q[0], not_32_out, and_5_out, not_31_out);
  LED led_1 (.in(decoder_1_out7));
  not not_34 (not_34_out, R_out);
  not not_35 (not_35_out, and_5_out);
  not not_36 (not_36_out, STATE_5_q[0]);
  and and_22 (and_22_out, STATE_5_q[2], not_36_out, and_1_out, not_35_out, not_34_out);
  or or_6 (or_7_out[1], and_21_out, and_22_out, and_24_out, and_23_out, and_25_out, and_31_out);
  LED led_2 (.in(decoder_1_out6));
  LED led_3 (.in(decoder_1_out1));
  LED led_4 (.in(decoder_1_out0));
  LED led_5 (.in(decoder_1_out4));
  not not_37 (not_37_out, R_out);
  not not_38 (not_38_out, R_out);
  and and_23 (and_23_out, STATE_5_q[1], and_1_out, and_5_out, not_38_out);
  and and_24 (and_24_out, STATE_5_q[1], STATE_5_q[0], not_37_out);
  or or_7 (or_7_out[0], and_26_out, and_27_out, and_28_out, and_29_out, and_30_out);
  LED led_6 (.in(decoder_1_out3));
  LED led_7 (.in(decoder_1_out2));
  not not_39 (not_39_out, and_5_out);
  not not_40 (not_40_out, and_1_out);
  not not_41 (not_41_out, STATE_5_q[2]);
  not not_42 (not_42_out, R_out);
  and and_25 (and_25_out, STATE_5_q[1], not_40_out, not_39_out, not_42_out);
  and and_26 (and_26_out, not_45_out, not_46_out, not_47_out, and_5_out, not_48_out);
  and and_27 (and_27_out, not_49_out, STATE_5_q[0], not_50_out, not_51_out, not_52_out);
  and and_28 (and_28_out, not_53_out, STATE_5_q[0], and_1_out, and_5_out, not_54_out);
  and and_29 (and_29_out, STATE_5_q[1], and_1_out, not_55_out, not_56_out);
  and and_30 (and_30_out, STATE_5_q[1], STATE_5_q[0], not_57_out);
  Decoder #(.select(3)) decoder_1 (
    .out0(decoder_1_out0), .out1(decoder_1_out1), .out2(decoder_1_out2), .out3(decoder_1_out3),
    .out4(decoder_1_out4), .out6(decoder_1_out6), .out7(decoder_1_out7), .sel(STATE_5_q));  // open: out5, en
  not not_43 (not_43_out, and_1_out);
  not not_44 (not_44_out, R_out);
  and and_31 (and_31_out, not_41_out, STATE_5_q[1], not_43_out, not_44_out);
  and and_32 (and_32_out, STATE_5_q[2], STATE_5_q[1], STATE_5_q[0]);
  and and_33 (and_33_out, not_58_out, STATE_5_q[1], STATE_5_q[0]);
  not not_45 (not_45_out, STATE_5_q[2]);
  not not_46 (not_46_out, STATE_5_q[0]);
  not not_47 (not_47_out, and_1_out);
  not not_48 (not_48_out, R_out);
  not not_49 (not_49_out, STATE_5_q[2]);
  not not_50 (not_50_out, and_1_out);
  not not_51 (not_51_out, and_5_out);
  not not_52 (not_52_out, R_out);
  not not_53 (not_53_out, STATE_5_q[2]);
  not not_54 (not_54_out, R_out);
  not not_55 (not_55_out, and_5_out);
  not not_56 (not_56_out, R_out);
  not not_57 (not_57_out, R_out);
  not not_58 (not_58_out, STATE_5_q[2]);

  // Notes on the sheet:
  //   Player 1 Button
  //   Player 2 Button
  //   Reset Button
  //   First Player Score
  //   Score Reset Button
  //   Second Player Score
  //   Lamps
endmodule
